# Fritzing sketch HBridgeSetup (saved by Fritzing 0.7.0b)
breadboards: 1

parts:
  IC1 = H-Bridge [package=THT]
  VCC1 = Battery
  M1 = DC Motor

nets:
  N1: IC1.1_2EN, IC1.3_4EN, IC1.VCC1
  GND1: IC1.GND1, IC1.GND2, IC1.GND3, IC1.GND4, VCC1.-
  N2: IC1.VCC2, VCC1.+
  N3: IC1.3Y, M1.pin_2
  N4: IC1.4Y, M1.pin_1

notes:
  To Arduino Pin
  Linked to DC Motor
  Arduino GND
  Arduino 5V
